// Logisim project Remainder.circ as structural Verilog
module Remainder (
  input  Sign_1,
  input  A,
  input  B,
  input  Sign_2,
  input  C,
  input  D,
  output out_7
);

  wire AB_out, AD_out, BC_2_out, BC_out, CD_out, CHECK0_out, n7_segment_display_driver_1_p5,
       n7_segment_display_driver_1_p6, n7_segment_display_driver_1_p7, n7_segment_display_driver_1_p8,
       n7_segment_display_driver_1_p9, n7_segment_display_driver_1_p10, n7_segment_display_driver_1_p11,
       not_1_out, TENS_out, UNITS_out;

  not not_1 (not_1_out, B);
  and BC (BC_out, B, C);
  and CD (CD_out, C, D);
  nand AD (AD_out, D, A);
  nor nor_1 (out_7, D, C);
  and UNITS (UNITS_out, BC_out, AD_out);
  and AB (AB_out, A, not_1_out);
  and TENS (TENS_out, AB_out, CD_out);
  or CHECK0 (CHECK0_out, TENS_out, UNITS_out);
  and BC_2 (BC_2_out, Sign_1, CHECK0_out);
  // _7_segment_display_driver 7_segment_display_driver_1: pin names not known; wires that end beside it: 1'b0, 1'b0, TENS_out, UNITS_out, n7_segment_display_driver_1_p5, n7_segment_display_driver_1_p6, n7_segment_display_driver_1_p7, n7_segment_display_driver_1_p8, n7_segment_display_driver_1_p9, n7_segment_display_driver_1_p10, n7_segment_display_driver_1_p11
  _7_Segment_Display u_7_segment_display_1 (
    .g(BC_2_out), .f(1'b0), .a(1'b0), .b(1'b0), .e(1'b0), .d(1'b0), .c(1'b0), .dp(1'b0));
  _7_Segment_Display u_7_segment_display_2 (
    .g(n7_segment_display_driver_1_p11), .f(n7_segment_display_driver_1_p10),
    .a(n7_segment_display_driver_1_p5), .b(n7_segment_display_driver_1_p6),
    .e(n7_segment_display_driver_1_p9), .d(n7_segment_display_driver_1_p8), .c(n7_segment_display_driver_1_p7));  // open: dp
endmodule
